// Logisim project 01-2to4_decoder.circ as structural Verilog: 1 circuit, main circuit main
module main (
  input  E,
  input  A,
  input  B
);

  wire nor_1_out, nor_2_out, nor_3_out, nor_4_out, nor_5_out, nor_6_out, nor_7_out;

  nor nor_1 (nor_1_out, E, E);
  nor nor_2 (nor_2_out, A, A);
  nor nor_3 (nor_3_out, B, B);
  nor nor_4 (nor_4_out, B, A, nor_1_out);
  nor nor_5 (nor_5_out, B, nor_2_out, nor_1_out);
  nor nor_6 (nor_6_out, nor_3_out, A, nor_1_out);
  nor nor_7 (nor_7_out, nor_3_out, nor_2_out, nor_1_out);
  LED led_1 (.in(nor_4_out));
  LED led_2 (.in(nor_5_out));
  LED led_3 (.in(nor_6_out));
  LED led_4 (.in(nor_7_out));

  // Notes on the sheet:
  //   E'
  //   A'
  //   B'
  //   D0
  //   D1
  //   D2
  //   D3
endmodule
