// Logisim project 3-4Bit_Adder.circ as structural Verilog: 1 circuit, main circuit main
module main (
  input  B0,
  input  B1,
  input  B2,
  input  B3,
  input  K,
  input  A0,
  input  A1,
  input  A2,
  input  A3
);

  wire adder_1_cout, adder_1_out, adder_2_cout, adder_2_out, adder_3_cout, adder_3_out, adder_4_cout,
       adder_4_out, xor_1_out, xor_2_out, xor_3_out, xor_4_out;

  xor xor_1 (xor_1_out, K, B0);
  Adder #(.width(1)) adder_1 (.a(xor_1_out), .b(A0), .out(adder_1_out), .cin(K), .cout(adder_1_cout));
  LED led_1 (.in(adder_1_out));
  xor xor_2 (xor_2_out, K, B1);
  Adder #(.width(1)) adder_2 (.a(xor_2_out), .b(A1), .out(adder_2_out), .cin(adder_1_cout), .cout(adder_2_cout));
  LED led_2 (.in(adder_2_out));
  xor xor_3 (xor_3_out, K, B2);
  Adder #(.width(1)) adder_3 (.a(xor_3_out), .b(A2), .out(adder_3_out), .cin(adder_2_cout), .cout(adder_3_cout));
  LED led_3 (.in(adder_3_out));
  xor xor_4 (xor_4_out, K, B3);
  LED led_4 (.in(adder_4_cout));
  Adder #(.width(1)) adder_4 (.a(xor_4_out), .b(A3), .out(adder_4_out), .cin(adder_3_cout), .cout(adder_4_cout));
  LED led_5 (.in(adder_4_out));

  // Notes on the sheet:
  //   S0
  //   S1
  //   S2
  //   C
  //   S3
endmodule
